// Logisim project FPA.circ as structural Verilog: 1 circuit, main circuit main
module main (
  input  [31:0] A,
  input  [31:0] B,
  output Overflow,
  output Underflow,
  output [31:0] out_5
);

  wire input_processing_handler_1_large_sign, input_processing_handler_1_small_sign, normalizer_1_overflow,
       rounder_1_out_3, significand_adder_1_carry_out, significand_adder_1_sign_bit;
  wire [8:0] input_processing_handler_1_large_exp, normalizer_1_normalized_exponent,
       rounded_normalizer_1_changed_exponent;
  wire [31:0] input_processing_handler_1_l_significant, input_processing_handler_1_s_significant,
       normalizer_1_normalized_significant, rounded_normalizer_1_changed_significant,
       rounder_1_rounded_significand, significand_adder_1_result;

  Input_Processing_Handler input_processing_handler_1 (
    .A(A), .B(B), .L_significant(input_processing_handler_1_l_significant),
    .S_significant(input_processing_handler_1_s_significant),
    .LARGE_EXP(input_processing_handler_1_large_exp), .LARGE_SIGN(input_processing_handler_1_large_sign),
    .SMALL_SIGN(input_processing_handler_1_small_sign));  // open: Ea_nEb
  Significand_Adder significand_adder_1 (
    .L_Sig(input_processing_handler_1_l_significant), .S_Sig(input_processing_handler_1_s_significant),
    .L_Sign(input_processing_handler_1_large_sign), .S_Sign(input_processing_handler_1_small_sign),
    .Result(significand_adder_1_result), .Carry_Out(significand_adder_1_carry_out),
    .Sign_Bit(significand_adder_1_sign_bit));
  Normalizer normalizer_1 (
    .Significand_input(significand_adder_1_result), .Exponent_Input(input_processing_handler_1_large_exp),
    .Carry(significand_adder_1_carry_out), .Normalized_Significant(normalizer_1_normalized_significant),
    .Normalized_Exponent(normalizer_1_normalized_exponent), .Overflow(normalizer_1_overflow),
    .Underflow(Underflow));
  Rounder rounder_1 (
    .significand(normalizer_1_normalized_significant), .rounded_significand(rounder_1_rounded_significand),
    .out_3(rounder_1_out_3));
  Rounded_Normalizer rounded_normalizer_1 (
    .Significant(rounder_1_rounded_significand), .Carry(rounder_1_out_3),
    .Exponent(normalizer_1_normalized_exponent), .Overflow(normalizer_1_overflow),
    .changed_Significant(rounded_normalizer_1_changed_significant),
    .changed_Exponent(rounded_normalizer_1_changed_exponent), .overflow_2(Overflow));
  // Output output_1: pin names not known; wires that end beside it: rounded_normalizer_1_changed_significant, rounded_normalizer_1_changed_exponent, significand_adder_1_sign_bit, out_5
endmodule
