// Logisim project A1_Group5.circ as structural Verilog: 10 circuits, main circuit Full Circuit
module Full_Circuit (
  input  [31:0] A,
  input  [31:0] B,
  output [25:0] Initial_Significand,
  output [10:0] out_4,
  output [25:0] Adjusted_Significand,
  output [4:0] Shift_amount,
  output [10:0] Final_Exponent,
  output [19:0] Final_Fraction,
  output Final_Sign_Bit,
  output Fraction_Zero_Flag,
  output [31:0] Final_Output,
  output Overflow,
  output Underflow
);

  wire Adjust_Exponent_exponent_overflow, Adjust_Exponent_negative_flag, Comparator_x__y,
       Rounding_Circuit_extra_shift_flag;
  wire [10:0] Comparator_difference;
  wire [25:0] Adjust_Input_2_adjusted_number, Adjust_Input_adjusted_number, Normalizer_normalized_significand;

  Comparator Comparator (
    .Exponent_A(A[30:20]), .Exponent_B(B[30:20]), .X__Y(Comparator_x__y), .Difference(Comparator_difference),
    .Larger_Exponent(out_4));  // open: X_Y
  Adjust_Exponent Adjust_Exponent (
    .Denormaliz_Flag(Rounding_Circuit_extra_shift_flag), .Larger_Exponent(out_4),
    .Shifting_amount(Shift_amount), .All_zero_flag(Fraction_Zero_Flag), .Final_Exponent(Final_Exponent),
    .Exponent_Overflow(Adjust_Exponent_exponent_overflow), .Negative_Flag(Adjust_Exponent_negative_flag));
  Adjust_Input Adjust_Input (
    .Input_Number({3'b001, A[19:0], 3'b000}), .Sign_Bit(A[31]), .Adjusted_Number(Adjust_Input_adjusted_number));
  Over_Underflow Over_underflow (
    .Final_Exponent(Final_Exponent), .Exponent_Overflow(Adjust_Exponent_exponent_overflow),
    .Fraction_Zero_Flag(Fraction_Zero_Flag), .Exponent_Neg(Adjust_Exponent_negative_flag),
    .Overflow(Overflow), .Underflow(Underflow));
  Significand_Adder Significand_Adder (
    .Significand_A(Adjust_Input_adjusted_number), .Significand_B(Adjust_Input_2_adjusted_number),
    .X__Y(Comparator_x__y), .Shifiting_amount(Comparator_difference), .Inital_Significand(Initial_Significand));
  Rounding_Circuit Rounding_Circuit (
    .Final_Significand(Normalizer_normalized_significand), .Final_Fraction_bits(Final_Fraction),
    .Extra_Shift_Flag(Rounding_Circuit_extra_shift_flag));
  Adjusting_sign_bit Adjusting_sign_bit (
    .Initial_Significand(Initial_Significand), .Adjusted_Significand(Adjusted_Significand),
    .Sign_bit(Final_Output[31]));
  Normailzation Normalizer (
    .Unnormalized_Significand(Adjusted_Significand),
    .Normalized_Significand(Normalizer_normalized_significand), .Shift_amount(Shift_amount),
    .Fraction_Zero(Fraction_Zero_Flag));
  Adjust_Input Adjust_Input_2 (
    .Input_Number({3'b001, B[19:0], 3'b000}), .Sign_Bit(B[31]),
    .Adjusted_Number(Adjust_Input_2_adjusted_number));

  assign Final_Output[30:0] = {Final_Exponent, Final_Fraction};
  assign Final_Sign_Bit = Final_Output[31];
endmodule

module Adjust_Input (
  input  [25:0] Input_Number,
  input  Sign_Bit,
  output [25:0] Adjusted_Number
);

  wire [25:0] negator_1_out;

  Negator #(.width(26)) negator_1 (.in(Input_Number), .out(negator_1_out));
  Multiplexer #(.width(26), .disabled(0), .enable("false")) multiplexer_1 (
    .in0(Input_Number), .in1(negator_1_out), .out(Adjusted_Number), .sel(Sign_Bit));
endmodule

module Comparator (
  input  [10:0] Exponent_A,
  input  [10:0] Exponent_B,
  output X__Y,
  output X_Y,
  output [10:0] Difference,
  output [10:0] Larger_Exponent
);

  wire comparator_1_eq, comparator_1_gt;
  wire [10:0] multiplexer_1_out;

  Comparator_part #(.width(11), .mode("unsigned")) comparator_1 (
    .a(Exponent_A), .b(Exponent_B), .gt(comparator_1_gt), .eq(comparator_1_eq), .lt(X_Y));
  or or_1 (X__Y, comparator_1_gt, comparator_1_eq);
  Multiplexer #(.width(11), .disabled(0), .enable("false")) multiplexer_1 (
    .in0(Exponent_A), .in1(Exponent_B), .out(multiplexer_1_out), .sel(X__Y));
  Multiplexer #(.width(11), .disabled(0), .enable("false")) multiplexer_2 (
    .in0(Exponent_A), .in1(Exponent_B), .out(Larger_Exponent), .sel(X_Y));
  Subtractor #(.width(11)) subtractor_1 (
    .a(Larger_Exponent), .b(multiplexer_1_out), .out(Difference), .bin(1'b0));  // open: bout

  // Notes on the sheet:
  //   X>=Y
  //   smaller
  //   larger
  //   larger - smaller
endmodule

module Significand_Adder (
  input  [25:0] Significand_A,
  input  [25:0] Significand_B,
  input  X__Y,
  input  [10:0] Shifiting_amount,
  output [25:0] Inital_Significand
);

  wire not_1_out, or_1_out;
  wire [25:0] multiplexer_1_out, multiplexer_2_out, multiplexer_3_out, shifter_1_out;

  Multiplexer #(.width(26), .disabled(0), .enable("false")) multiplexer_1 (
    .in0(Significand_A), .in1(Significand_B), .out(multiplexer_1_out), .sel(X__Y));
  not not_1 (not_1_out, X__Y);
  Shifter #(.width(26), .shift("ar")) shifter_1 (
    .in(multiplexer_1_out), .\dist (Shifiting_amount[4:0]), .out(shifter_1_out));
  Multiplexer #(.width(26), .disabled(0), .enable("false")) multiplexer_2 (
    .in0(Significand_A), .in1(Significand_B), .out(multiplexer_2_out), .sel(not_1_out));
  or or_1 (or_1_out, Shifiting_amount[5], Shifiting_amount[6], Shifiting_amount[7], Shifiting_amount[8], Shifiting_amount[9], Shifiting_amount[10]);
  Multiplexer #(.width(26), .enable("false")) multiplexer_3 (
    .in0(shifter_1_out), .in1({26{1'b0}}), .out(multiplexer_3_out), .sel(or_1_out));
  Adder #(.width(26)) adder_1 (
    .a(multiplexer_2_out), .b(multiplexer_3_out), .out(Inital_Significand), .cin(1'b0));  // open: cout

  // Notes on the sheet:
  //   Smaller
  //   Larger
endmodule

module Adjusting_sign_bit (
  input  [25:0] Initial_Significand,
  output [25:0] Adjusted_Significand,
  output Sign_bit
);

  wire [25:0] adder_1_out, not_1_out;

  assign not_1_out = ~Initial_Significand;  // NOT_Gate not_1, 26 bits wide
  Adder #(.width(26)) adder_1 (.a(not_1_out), .b(26'h1), .out(adder_1_out), .cin(1'b0));  // open: cout
  Multiplexer #(.width(26), .enable("false")) multiplexer_1 (
    .in0(Initial_Significand), .in1(adder_1_out), .out(Adjusted_Significand), .sel(Initial_Significand[25]));

  assign Sign_bit = Initial_Significand[25];
endmodule

module Normailzation (
  input  [25:0] Unnormalized_Significand,
  output [25:0] Normalized_Significand,
  output [4:0] Shift_amount,
  output Fraction_Zero
);

  wire priority_encoder_1_gs;
  wire [4:0] multiplexer_1_out, priority_encoder_1_out;
  wire [31:0] bit_extender_1_out;

  assign bit_extender_1_out = {{6{1'b0}}, Unnormalized_Significand};  // Bit_Extender bit_extender_1
  Priority_Encoder #(.select(5), .disabled(0)) priority_encoder_1 (
    .in0(bit_extender_1_out[0]), .in1(bit_extender_1_out[1]), .in2(bit_extender_1_out[2]),
    .in3(bit_extender_1_out[3]), .in4(bit_extender_1_out[4]), .in5(bit_extender_1_out[5]),
    .in6(bit_extender_1_out[6]), .in7(bit_extender_1_out[7]), .in8(bit_extender_1_out[8]),
    .in9(bit_extender_1_out[9]), .in10(bit_extender_1_out[10]), .in11(bit_extender_1_out[11]),
    .in12(bit_extender_1_out[12]), .in13(bit_extender_1_out[13]), .in14(bit_extender_1_out[14]),
    .in15(bit_extender_1_out[15]), .in16(bit_extender_1_out[16]), .in17(bit_extender_1_out[17]),
    .in18(bit_extender_1_out[18]), .in19(bit_extender_1_out[19]), .in20(bit_extender_1_out[20]),
    .in21(bit_extender_1_out[21]), .in22(bit_extender_1_out[22]), .in23(bit_extender_1_out[23]),
    .in24(bit_extender_1_out[24]), .in25(bit_extender_1_out[25]), .in26(bit_extender_1_out[26]),
    .in27(bit_extender_1_out[27]), .in28(bit_extender_1_out[28]), .in29(bit_extender_1_out[29]),
    .in30(bit_extender_1_out[30]), .in31(bit_extender_1_out[31]), .out(priority_encoder_1_out),
    .gs(priority_encoder_1_gs), .en_in(1'b1));  // open: en_out
  not not_1 (Fraction_Zero, priority_encoder_1_gs);
  Multiplexer #(.width(5), .enable("false")) multiplexer_1 (
    .in0(priority_encoder_1_out), .in1(5'b10111), .out(multiplexer_1_out), .sel(Fraction_Zero));
  Subtractor #(.width(5)) subtractor_1 (
    .a(5'b11001), .b(multiplexer_1_out), .out(Shift_amount), .bin(1'b0));  // open: bout
  Shifter #(.width(26)) shifter_1 (.in(Unnormalized_Significand), .\dist (Shift_amount), .out(Normalized_Significand));
endmodule

module Rounding_Circuit (
  input  [25:0] Final_Significand,
  output [19:0] Final_Fraction_bits,
  output Extra_Shift_Flag
);

  wire and_1_out, or_1_out;
  wire [19:0] bit_extender_1_out;

  or or_1 (or_1_out, Final_Significand[0], Final_Significand[1], Final_Significand[2], Final_Significand[3], Final_Significand[5]);
  and and_1 (and_1_out, or_1_out, Final_Significand[4]);
  assign bit_extender_1_out = {{19{1'b0}}, and_1_out};  // Bit_Extender bit_extender_1
  Adder #(.width(20)) adder_1 (
    .a(bit_extender_1_out), .b(Final_Significand[24:5]), .out(Final_Fraction_bits), .cin(1'b0),
    .cout(Extra_Shift_Flag));
endmodule

module Adjust_Exponent (
  input  Denormaliz_Flag,
  input  [10:0] Larger_Exponent,
  input  [4:0] Shifting_amount,
  input  All_zero_flag,
  output [10:0] Final_Exponent,
  output Exponent_Overflow,
  output Negative_Flag
);

  wire [11:0] adder_1_out, subtractor_1_out;

  Adder #(.width(12)) adder_1 (
    .a({1'b0, Larger_Exponent}), .b(12'h2), .out(adder_1_out), .cin(Denormaliz_Flag));  // open: cout
  Subtractor #(.width(12)) subtractor_1 (
    .a(adder_1_out), .b({{7{1'b0}}, Shifting_amount}), .out(subtractor_1_out), .bin(1'b0),
    .bout(Negative_Flag));
  Multiplexer #(.width(12), .enable("false")) multiplexer_1 (
    .in0(subtractor_1_out), .in1({12{1'b0}}), .out({Exponent_Overflow, Final_Exponent}), .sel(All_zero_flag));
endmodule

module Over_Underflow (
  input  [10:0] Final_Exponent,
  input  Exponent_Overflow,
  input  Fraction_Zero_Flag,
  input  Exponent_Neg,
  output Overflow,
  output Underflow
);

  wire and_1_out, and_2_out, nor_1_out, not_1_out;

  not not_1 (not_1_out, Exponent_Overflow);
  and and_1 (and_1_out, Final_Exponent[0], Final_Exponent[1], Final_Exponent[2], Final_Exponent[3], Final_Exponent[4], Final_Exponent[5], Final_Exponent[6], Final_Exponent[7], Final_Exponent[8], Final_Exponent[9], Final_Exponent[10]);
  nor nor_1 (nor_1_out, Final_Exponent[10], Final_Exponent[9], Final_Exponent[8], Final_Exponent[7], Final_Exponent[6], Final_Exponent[5], Final_Exponent[4], Final_Exponent[3], Final_Exponent[2], Final_Exponent[1], Final_Exponent[0]);
  and and_2 (and_2_out, nor_1_out, not_1_out);
  or or_1 (Overflow, and_1_out, Exponent_Overflow);
  or or_2 (Underflow, and_2_out, Fraction_Zero_Flag, Exponent_Neg);
endmodule

module FPA_IC (
  input  [31:0] Input_A,
  input  [31:0] Input_B,
  output [31:0] Output_Number,
  output Underflow_Flag,
  output Overflow_Flag
);

  Full_Circuit full_circuit_1 (
    .A(Input_B), .B(Input_A), .Final_Output(Output_Number), .Overflow(Overflow_Flag),
    .Underflow(Underflow_Flag));  // open: Shift_amount, Final_Fraction, Fraction_Zero_Flag, Final_Sign_Bit, Initial_Significand, out_4, Adjusted_Significand, Final_Exponent
endmodule
