// Logisim project Normalizer.circ as structural Verilog: 3 circuits, main circuit Normalizer
module Normalizer (
  input  [31:0] Significand_input,
  input  [8:0] Exponent_Input,
  input  Carry,
  output [31:0] Normalized_Significant,
  output [8:0] Normalized_Exponent,
  output Overflow,
  output Underflow
);

  wire adder_subtractor_1_overflow, adder_subtractor_1_underflow, and_1_out, multiplexer_4_out, not_1_out,
       One_p2, priority_encoder_1_en_out;
  wire [4:0] multiplexer_1_out, multiplexer_2_out, priority_encoder_1_out;
  wire [8:0] adder_subtractor_1_output_exponent;
  wire [31:0] shifter_1_output;

  Priority_Encoder #(.select(5)) priority_encoder_1 (
    .in0(Significand_input[31]), .in1(Significand_input[30]), .in2(Significand_input[29]),
    .in3(Significand_input[28]), .in4(Significand_input[27]), .in5(Significand_input[26]),
    .in6(Significand_input[25]), .in7(Significand_input[24]), .in8(Significand_input[23]),
    .in9(Significand_input[22]), .in10(Significand_input[21]), .in11(Significand_input[20]),
    .in12(Significand_input[19]), .in13(Significand_input[18]), .in14(Significand_input[17]),
    .in15(Significand_input[16]), .in16(Significand_input[15]), .in17(Significand_input[14]),
    .in18(Significand_input[13]), .in19(Significand_input[12]), .in20(Significand_input[11]),
    .in21(Significand_input[10]), .in22(Significand_input[9]), .in23(Significand_input[8]),
    .in24(Significand_input[7]), .in25(Significand_input[6]), .in26(Significand_input[5]),
    .in27(Significand_input[4]), .in28(Significand_input[3]), .in29(Significand_input[2]),
    .in30(Significand_input[1]), .in31(Significand_input[0]), .out(priority_encoder_1_out),
    .en_out(priority_encoder_1_en_out), .en_in(1'b1));  // open: gs
  not not_1 (not_1_out, Carry);
  and and_1 (and_1_out, priority_encoder_1_en_out, not_1_out);
  Multiplexer #(.width(5), .enable("false")) multiplexer_1 (
    .in0(multiplexer_2_out), .in1(5'b00001), .out(multiplexer_1_out), .sel(Carry));
  Multiplexer #(.width(5), .disabled(0), .enable("false")) multiplexer_2 (
    .in0(priority_encoder_1_out), .in1({5{1'b0}}), .out(multiplexer_2_out), .sel(Carry));
  Shifter shifter_1 (
    .Input(Significand_input), .Shift_Amount(multiplexer_2_out), .Left_Right(Carry), .Output(shifter_1_output));
  Adder_Subtractor adder_subtractor_1 (
    .Exponent(Exponent_Input), .Add_Sub_amount(multiplexer_1_out), .overflow(adder_subtractor_1_overflow),
    .Add_sub(Carry), .underflow(adder_subtractor_1_underflow),
    .output_exponent(adder_subtractor_1_output_exponent));
  Multiplexer #(.width(32), .disabled(0), .enable("false")) multiplexer_3 (
    .in0(shifter_1_output), .in1({32{1'b0}}), .out(Normalized_Significant), .sel(priority_encoder_1_en_out));
  Multiplexer #(.disabled(0), .enable("false")) multiplexer_4 (
    .in0(adder_subtractor_1_overflow), .in1(1'b0), .out(multiplexer_4_out), .sel(priority_encoder_1_en_out));
  Multiplexer #(.width(9), .disabled(0), .enable("false")) multiplexer_5 (
    .in0(adder_subtractor_1_output_exponent), .in1({9{1'b0}}), .out(Normalized_Exponent), .sel(and_1_out));
  // _1_cheacker One: pin names not known; wires that end beside it: Normalized_Exponent, One_p2
  or or_1 (Overflow, One_p2, multiplexer_4_out);
  Multiplexer #(.disabled(0), .enable("false")) multiplexer_6 (
    .in0(adder_subtractor_1_underflow), .in1(1'b0), .out(Underflow), .sel(priority_encoder_1_en_out));
endmodule

module Shifter (
  input  [31:0] Input,
  input  Left_Right,
  input  [4:0] Shift_Amount,
  output [31:0] Output
);

  wire [31:0] arbitary_rightshifter_1_output, arbitrary_leftshifter_1_p3;

  // arbitrary_leftShifter arbitrary_leftshifter_1: pin names not known; wires that end beside it: Input, Shift_Amount, arbitrary_leftshifter_1_p3
  arbitary_rightShifter arbitary_rightshifter_1 (
    .\input (Input), .Shift_Amount(Shift_Amount), .\output (arbitary_rightshifter_1_output));
  Multiplexer #(.width(32), .disabled(0), .enable("false")) multiplexer_1 (
    .in0(arbitrary_leftshifter_1_p3), .in1(arbitary_rightshifter_1_output), .out(Output), .sel(Left_Right));
endmodule

// A/S
module Adder_Subtractor (
  input  [8:0] Exponent,
  input  [4:0] Add_Sub_amount,
  input  Add_sub,
  output underflow,
  output [8:0] output_exponent,
  output overflow
);

  wire adder_1_cout, not_1_out, subtractor_1_bout;
  wire [8:0] adder_1_out, subtractor_1_out;

  Subtractor #(.width(9)) subtractor_1 (
    .a(Exponent), .b({4'b0000, Add_Sub_amount}), .out(subtractor_1_out), .bin(1'b0), .bout(subtractor_1_bout));
  Adder #(.width(9)) adder_1 (
    .a(Exponent), .b({4'b0000, Add_Sub_amount}), .out(adder_1_out), .cin(1'b0), .cout(adder_1_cout));
  and and_1 (overflow, adder_1_cout, Add_sub);
  not not_1 (not_1_out, Add_sub);
  and and_2 (underflow, not_1_out, subtractor_1_bout);
  Multiplexer #(.width(9), .disabled(0), .enable("false")) multiplexer_1 (
    .in0(subtractor_1_out), .in1(adder_1_out), .out(output_exponent), .sel(Add_sub));
endmodule
