// Logisim project Significand Adder.circ as structural Verilog: 1 circuit, main circuit Significand Adder
module Significand_Adder (
  input  [31:0] L_Sig,
  input  [31:0] S_Sig,
  input  L_Sign,
  input  S_Sign,
  output [31:0] Result,
  output Carry_Out,
  output Sign_Bit
);

  wire xor_1_out;

  xor xor_1 (xor_1_out, L_Sign, S_Sign);
  // ALU alu_1: pin names not known; wires that end beside it: L_Sig, S_Sig, xor_1_out, Result, Carry_Out

  assign Sign_Bit = S_Sign;
endmodule
