// Logisim project IPH2.circ as structural Verilog: 3 circuits, main circuit Input Processing Handler
module Input_Processing_Handler (
  input  [31:0] A,
  input  [31:0] B,
  output [31:0] L_significant,
  output [31:0] S_significant,
  output [8:0] Ea_nEb,
  output [8:0] LARGE_EXP,
  output LARGE_SIGN,
  output SMALL_SIGN
);

  wire exp_process_1_ea_eb, input_process_1_sign_bit, input_process_2_sign_bit;
  wire [8:0] input_process_1_exponential, input_process_2_exponential;
  wire [31:0] input_process_1_output_number, input_process_2_output_number, multiplexer_2_out;

  Input_process input_process_1 (
    .exponential(input_process_1_exponential), .in_1(A), .output_number(input_process_1_output_number),
    .sign_bit(input_process_1_sign_bit));
  Input_process input_process_2 (
    .exponential(input_process_2_exponential), .in_1(B), .output_number(input_process_2_output_number),
    .sign_bit(input_process_2_sign_bit));
  Exp_process exp_process_1 (
    .Ea(input_process_1_exponential), .Eb(input_process_2_exponential), .Sa(input_process_1_sign_bit),
    .Sb(input_process_2_sign_bit), .Smaller_s_sign(SMALL_SIGN), .Ea_Eb(exp_process_1_ea_eb), .Ea_nEb(Ea_nEb),
    .Large_exp(LARGE_EXP), .Larger_s_sign(LARGE_SIGN));
  Multiplexer #(.width(32)) multiplexer_1 (
    .in0(input_process_2_output_number), .in1(input_process_1_output_number), .out(L_significant),
    .sel(exp_process_1_ea_eb), .en(1'b1));
  Multiplexer #(.width(32)) multiplexer_2 (
    .in0(input_process_1_output_number), .in1(input_process_2_output_number), .out(multiplexer_2_out),
    .sel(exp_process_1_ea_eb), .en(1'b1));
  rightShifter rightshifter_1 (.significand(multiplexer_2_out), .\output (S_significant), .exponent_difference(Ea_nEb));
endmodule

// ExpP
module Exp_process (
  input  [8:0] Ea,
  input  [8:0] Eb,
  input  Sa,
  input  Sb,
  output Ea_Eb,
  output [8:0] Ea_nEb,
  output [8:0] Large_exp,
  output Larger_s_sign,
  output Smaller_s_sign
);

  wire [8:0] multiplexer_2_out;

  Comparator #(.width(9), .mode("unsigned")) comparator_1 (.a(Ea), .b(Eb), .gt(Ea_Eb));  // open: eq, lt
  Multiplexer #(.width(9)) multiplexer_1 (.in0(Eb), .in1(Ea), .out(Large_exp), .sel(Ea_Eb), .en(1'b1));
  Multiplexer #(.width(9)) multiplexer_2 (.in0(Ea), .in1(Eb), .out(multiplexer_2_out), .sel(Ea_Eb), .en(1'b1));
  Multiplexer multiplexer_3 (.in0(Sb), .in1(Sa), .out(Larger_s_sign), .sel(Ea_Eb), .en(1'b1));
  Multiplexer multiplexer_4 (.in0(Sa), .in1(Sb), .out(Smaller_s_sign), .sel(Ea_Eb), .en(1'b1));
  Subtractor #(.width(9)) subtractor_1 (.a(Large_exp), .b(multiplexer_2_out), .out(Ea_nEb));  // open: bin, bout
endmodule

// IP
module Input_process (
  input  [31:0] in_1,
  output [31:0] output_number,
  output [8:0] exponential,
  output sign_bit
);


  assign exponential = in_1[30:22];
  assign output_number = {1'b1, in_1[21:0], {9{1'b0}}};
  assign sign_bit = in_1[31];
endmodule
