// Logisim project Right_shift.circ as structural Verilog
// 1
module _1_bit (
  input  [31:0] Input,
  input  Enable,
  output [31:0] _1_bit_shifted
);

  Multiplexer #(.width(32)) multiplexer_1 (
    .in0(Input), .in1({1'b0, Input[31:1]}), .out(_1_bit_shifted), .sel(Enable), .en(1'b1));
endmodule

// 2
module _2_bit (
  input  [31:0] Input,
  input  Enable,
  output [31:0] _2_bit_shifted
);

  Multiplexer #(.width(32)) multiplexer_1 (
    .in0(Input), .in1({2'b00, Input[31:2]}), .out(_2_bit_shifted), .sel(Enable), .en(1'b1));
endmodule

// 4
module _4_bit (
  input  [31:0] Input,
  input  Enable,
  output [31:0] _4_bit_shifted
);

  Multiplexer #(.width(32)) multiplexer_1 (
    .in0(Input), .in1({4'b0000, Input[31:4]}), .out(_4_bit_shifted), .sel(Enable), .en(1'b1));
endmodule

// 8
module _8_bit (
  input  [31:0] Input,
  input  Enable,
  output [31:0] _8_bit_shifted
);

  Multiplexer #(.width(32)) multiplexer_1 (
    .in0(Input), .in1({{8{1'b0}}, Input[31:8]}), .out(_8_bit_shifted), .sel(Enable), .en(1'b1));
endmodule

// 16
module _16_bit (
  input  [31:0] Input,
  input  Enable,
  output [31:0] _16_bit_shifted
);

  Multiplexer #(.width(32)) multiplexer_1 (
    .in0(Input), .in1({{16{1'b0}}, Input[31:16]}), .out(_16_bit_shifted), .sel(Enable), .en(1'b1));
endmodule

// A/S
module Arbiary_shifter (
  input  [31:0] Input,
  input  [4:0] Shifting_amount,
  output [31:0] Shited_output
);

  wire [31:0] n1_bit_1__1_bit_shifted, n2_bit_1__2_bit_shifted, n4_bit_1__4_bit_shifted,
       n8_bit_1__8_bit_shifted;

  _1_bit u_1_bit_1 (.Input(Input), .Enable(Shifting_amount[0]), ._1_bit_shifted(n1_bit_1__1_bit_shifted));
  _2_bit u_2_bit_1 (
    .Input(n1_bit_1__1_bit_shifted), .Enable(Shifting_amount[1]), ._2_bit_shifted(n2_bit_1__2_bit_shifted));
  _4_bit u_4_bit_1 (
    .Input(n2_bit_1__2_bit_shifted), .Enable(Shifting_amount[2]), ._4_bit_shifted(n4_bit_1__4_bit_shifted));
  _8_bit u_8_bit_1 (
    .Input(n4_bit_1__4_bit_shifted), .Enable(Shifting_amount[3]), ._8_bit_shifted(n8_bit_1__8_bit_shifted));
  _16_bit u_16_bit_1 (.Input(n8_bit_1__8_bit_shifted), .Enable(Shifting_amount[4]), ._16_bit_shifted(Shited_output));
endmodule

module R_Shift (
  input  [31:0] input_number,
  input  [8:0] shiting_amount,
  output [31:0] shifted_output
);

  wire n7432_1__6__2y, n7432_1__8__3y, n7432_1__11__4y;
  wire [31:0] arbiary_shifter_1_shited_output;

  Arbiary_shifter arbiary_shifter_1 (
    .Input(input_number), .Shifting_amount(shiting_amount[4:0]),
    .Shited_output(arbiary_shifter_1_shited_output));
  _7432 u_7432_1 (
    ._4__2A(shiting_amount[5]), ._5__2B(n7432_1__8__3y), ._6__2Y(n7432_1__6__2y), ._7__GND(1'b0),
    ._14__Vcc(1'b1), ._13__4B(shiting_amount[8]), ._12__4A(shiting_amount[7]), ._11__4Y(n7432_1__11__4y),
    ._10__3B(n7432_1__11__4y), ._9__3A(shiting_amount[6]), ._8__3Y(n7432_1__8__3y));  // open: _1__1A, _2__1B, _3__1Y
  Multiplexer #(.width(32)) multiplexer_1 (
    .in0(arbiary_shifter_1_shited_output), .in1({32{1'b0}}), .out(shifted_output), .sel(n7432_1__6__2y),
    .en(1'b1));
endmodule
