// Logisim project RoundedNormalizer.circ as structural Verilog: 1 circuit, main circuit Rounded Normalizer
module Rounded_Normalizer (
  input  [31:0] Significant,
  input  Carry,
  input  [8:0] Exponent,
  input  Overflow,
  output [31:0] changed_Significant,
  output [8:0] changed_Exponent,
  output overflow_2
);

  wire comparator_1_eq;
  wire [8:0] adder_1_out;

  Multiplexer #(.width(32)) multiplexer_1 (
    .in0(Significant), .in1({32{1'b0}}), .out(changed_Significant), .sel(Carry), .en(1'b1));
  Multiplexer #(.width(9)) multiplexer_2 (
    .in0(Exponent), .in1(adder_1_out), .out(changed_Exponent), .sel(Carry), .en(1'b1));
  Adder #(.width(9)) adder_1 (.a(Exponent), .b({9{1'b0}}), .out(adder_1_out), .cin(Carry));  // open: cout
  Comparator #(.width(9), .mode("unsigned")) comparator_1 (
    .a(changed_Exponent), .b({9{1'b1}}), .eq(comparator_1_eq));  // open: gt, lt
  or or_1 (overflow_2, comparator_1_eq, Overflow);
endmodule
