// Logisim project Rounder.circ as structural Verilog: 2 circuits, main circuit Rounder
module Rounder (
  input  [31:0] significand,
  output [31:0] rounded_significand,
  output out_3
);

  wire or_1_out, or_2_out;
  wire [10:10] and_1_out;

  or or_1 (or_1_out, significand[0], significand[1], significand[2], significand[4], significand[5], significand[6], significand[7]);
  or or_2 (or_2_out, or_1_out, significand[8], significand[10]);
  and and_1 (and_1_out[10], or_2_out, significand[9]);
  Adder #(.width(32)) adder_1 (
    .a({{21{1'b0}}, and_1_out[10], {10{1'b0}}}), .b({significand[31:10], {10{1'b0}}}),
    .out(rounded_significand), .cin(1'b0), .cout(out_3));

  // Notes on the sheet:
  //   Cout=1(Denormalized)
endmodule

module sticky (
  input  [6:0] in_1
);

  // OR_Gate or_1 has open pins: in0=in_1[0], in1=in_1[1], in2=in_1[2], in3=in_1[3], in4=in_1[4], in5=in_1[5], in6=in_1[6], out=open
endmodule
